// Logisim project Half_step unipolar.circ as structural Verilog: 1 circuit, main circuit main
module main (
  input  in_1,
  output out_2,
  output out_3,
  output out_4,
  output out_5
);

  wire and_1_out, and_2_out, and_3_out, and_4_out, and_5_out, and_6_out, and_7_out, and_8_out, and_9_out,
       and_10_out, and_11_out, and_12_out, and_13_out, and_14_out, and_15_out, and_16_out, clock_1_out,
       j_k_ff_1_qn, j_k_ff_2_qn, j_k_ff_3_qn, j_k_ff_4_qn, not_3_out, or_1_out, or_2_out, or_3_out, or_4_out;

  // NOT_Gate not_1 is placed but not wired
  // NOT_Gate not_2 is placed but not wired
  and and_1 (and_1_out, out_2, out_5, in_1);
  and and_2 (and_2_out, out_2, out_3, not_3_out);
  and and_3 (and_3_out, j_k_ff_1_qn, j_k_ff_2_qn, j_k_ff_3_qn, not_3_out);
  and and_4 (and_4_out, j_k_ff_1_qn, j_k_ff_3_qn, j_k_ff_4_qn, in_1);
  and and_5 (and_5_out, out_3, out_4, not_3_out);
  and and_6 (and_6_out, out_2, out_3, in_1);
  and and_7 (and_7_out, j_k_ff_2_qn, out_4, j_k_ff_4_qn, in_1);
  and and_8 (and_8_out, out_2, j_k_ff_2_qn, j_k_ff_4_qn, not_3_out);
  and and_9 (and_9_out, out_4, out_5, not_3_out);
  and and_10 (and_10_out, out_3, out_4, in_1);
  and and_11 (and_11_out, j_k_ff_1_qn, j_k_ff_3_qn, out_5, in_1);
  and and_12 (and_12_out, j_k_ff_1_qn, out_3, j_k_ff_3_qn, not_3_out);
  and and_13 (and_13_out, out_4, out_5, in_1);
  and and_14 (and_14_out, out_2, out_5, not_3_out);
  and and_15 (and_15_out, j_k_ff_2_qn, out_4, j_k_ff_4_qn, not_3_out);
  and and_16 (and_16_out, out_2, j_k_ff_2_qn, j_k_ff_4_qn, in_1);
  or or_1 (or_1_out, and_1_out, and_2_out, and_3_out, and_4_out);
  or or_2 (or_2_out, and_5_out, and_6_out, and_7_out, and_8_out);
  or or_3 (or_3_out, and_9_out, and_10_out, and_11_out, and_12_out);
  or or_4 (or_4_out, and_13_out, and_14_out, and_15_out, and_16_out);
  Clock clock_1 (.out(clock_1_out));
  J_K_Flip_Flop j_k_ff_1 (
    .J(or_1_out), .clk(clock_1_out), .K(or_1_out), .Q(out_2), .Qn(j_k_ff_1_qn));  // open: preset, en, reset
  J_K_Flip_Flop j_k_ff_2 (
    .J(or_2_out), .clk(clock_1_out), .K(or_2_out), .Q(out_3), .Qn(j_k_ff_2_qn));  // open: preset, en, reset
  J_K_Flip_Flop j_k_ff_3 (
    .J(or_3_out), .clk(clock_1_out), .K(or_3_out), .Q(out_4), .Qn(j_k_ff_3_qn));  // open: preset, en, reset
  J_K_Flip_Flop j_k_ff_4 (
    .J(or_4_out), .clk(clock_1_out), .K(or_4_out), .Q(out_5), .Qn(j_k_ff_4_qn));  // open: preset, en, reset
  not not_3 (not_3_out, in_1);
  // NOT_Gate not_4 is placed but not wired
endmodule
