// Logisim project counter.circ as structural Verilog: 1 circuit, main circuit main
module main (
  input  in_1
);

  wire clock_1_out, j_k_ff_2_q, j_k_ff_3_q, j_k_ff_4_q, j_k_ff_5_q, j_k_ff_6_q, j_k_ff_7_q, j_k_ff_8_q;

  // NOT_Gate not_1 is placed but not wired
  // NOT_Gate not_2 is placed but not wired
  J_K_Flip_Flop #(.trigger("falling")) j_k_ff_1 (
    .J(in_1), .clk(j_k_ff_2_q), .K(in_1));  // open: Q, Qn, preset, en, reset
  J_K_Flip_Flop #(.trigger("falling")) j_k_ff_2 (
    .J(in_1), .clk(j_k_ff_3_q), .K(in_1), .Q(j_k_ff_2_q));  // open: Qn, preset, en, reset
  J_K_Flip_Flop #(.trigger("falling")) j_k_ff_3 (
    .J(in_1), .clk(j_k_ff_4_q), .K(in_1), .Q(j_k_ff_3_q));  // open: Qn, preset, en, reset
  J_K_Flip_Flop #(.trigger("falling")) j_k_ff_4 (
    .J(in_1), .clk(j_k_ff_5_q), .K(in_1), .Q(j_k_ff_4_q));  // open: Qn, preset, en, reset
  J_K_Flip_Flop #(.trigger("falling")) j_k_ff_5 (
    .J(in_1), .clk(j_k_ff_6_q), .K(in_1), .Q(j_k_ff_5_q));  // open: Qn, preset, en, reset
  J_K_Flip_Flop #(.trigger("falling")) j_k_ff_6 (
    .J(in_1), .clk(j_k_ff_7_q), .K(in_1), .Q(j_k_ff_6_q));  // open: Qn, preset, en, reset
  J_K_Flip_Flop #(.trigger("falling")) j_k_ff_7 (
    .J(in_1), .clk(j_k_ff_8_q), .K(in_1), .Q(j_k_ff_7_q));  // open: Qn, preset, en, reset
  J_K_Flip_Flop #(.trigger("falling")) j_k_ff_8 (
    .J(in_1), .clk(clock_1_out), .K(in_1), .Q(j_k_ff_8_q));  // open: Qn, preset, en, reset
  Clock clock_1 (.out(clock_1_out));
  // NOT_Gate not_3 is placed but not wired
endmodule
