// Logisim project bi-directional stepper driver.circ as structural Verilog: 1 circuit, main circuit main
module main (
  input  in_1,
  output out_2,
  output out_3,
  output out_4,
  output out_5
);

  wire and_1_out, and_2_out, and_3_out, and_4_out, and_5_out, and_6_out, and_7_out, and_8_out, clock_1_out,
       not_1_out, or_1_out, or_2_out, or_3_out, or_4_out;

  not not_1 (not_1_out, in_1);
  and and_1 (and_1_out, out_5, in_1);
  and and_2 (and_2_out, out_3, not_1_out);
  and and_3 (and_3_out, not_1_out, out_4);
  and and_4 (and_4_out, out_2, in_1);
  and and_5 (and_5_out, out_5, not_1_out);
  and and_6 (and_6_out, out_3, in_1);
  and and_7 (and_7_out, out_4, in_1);
  and and_8 (and_8_out, not_1_out, out_2);
  or or_1 (or_1_out, out_2, and_1_out, and_2_out);
  Clock clock_1 (.out(clock_1_out));
  or or_2 (or_2_out, out_3, and_3_out, and_4_out);
  or or_3 (or_3_out, out_4, and_5_out, and_6_out);
  or or_4 (or_4_out, out_5, and_7_out, and_8_out);
  J_K_Flip_Flop #(.trigger("falling")) j_k_ff_1 (
    .J(or_1_out), .clk(clock_1_out), .K(or_1_out), .Q(out_2));  // open: Qn, preset, en, reset
  J_K_Flip_Flop #(.trigger("falling")) j_k_ff_2 (
    .J(or_2_out), .clk(clock_1_out), .K(or_2_out), .Q(out_3));  // open: Qn, preset, en, reset
  J_K_Flip_Flop #(.trigger("falling")) j_k_ff_3 (
    .J(or_3_out), .clk(clock_1_out), .K(or_3_out), .Q(out_4));  // open: Qn, preset, en, reset
  J_K_Flip_Flop #(.trigger("falling")) j_k_ff_4 (
    .J(or_4_out), .clk(clock_1_out), .K(or_4_out), .Q(out_5));  // open: Qn, preset, en, reset
endmodule
