// Logisim project xnor_jk latch.circ as structural Verilog: 1 circuit, main circuit main
module main (
  input  in_1,
  input  in_2,
  input  in_3,
  input  in_4,
  output out_5,
  output out_6
);

  wire not_1_out, xnor_1_out, xor_1_out;

  xor xor_1 (xor_1_out, in_2, in_4);
  not not_1 (not_1_out, xor_1_out);
  J_K_Flip_Flop #(.trigger("falling")) j_k_ff_1 (
    .J(in_2), .clk(not_1_out), .K(in_4), .Q(out_6));  // open: Qn, preset, en, reset
  xnor xnor_1 (xnor_1_out, in_1, in_3);
  J_K_Flip_Flop #(.trigger("falling")) j_k_ff_2 (
    .J(in_1), .clk(xnor_1_out), .K(in_3), .Q(out_5));  // open: Qn, preset, en, reset
endmodule
